// Logisim project PROJECT2.circ as structural Verilog: 1 circuit, main circuit main
// AR
module main (
  input  [2:0] D2D1D0,
  input  [1:0] A1A0,
  input  in_3,
  input  in_4,
  input  in_5,
  input  in_6,
  input  in_7,
  input  in_8,
  input  in_9,
  input  in_10,
  input  in_11,
  input  in_12,
  input  in_13,
  input  in_14,
  input  in_15,
  input  in_16,
  input  in_17,
  input  in_18,
  input  in_19,
  input  in_20,
  input  in_21,
  input  in_22,
  input  in_23,
  input  in_24,
  input  [7:0] in_25,
  input  in_26,
  input  in_27,
  input  in_28,
  input  in_29,
  input  in_30,
  input  in_31,
  input  in_32,
  input  [3:0] S0S1S2S3,
  input  in_34,
  input  in_35,
  input  in_36,
  output [7:0] out_37
);

  wire AR_p4, GPRB_p6, n1_bit_real_alu_1_p3, n1_bit_real_alu_1_p6, X_p1, X_p2, X_p3, X_p8;
  wire [4:0] X_p10;
  wire [7:0] INPR_p6, IR_p1, IR_p1_2;
  wire [9:0] adder_1_out, AR_p6, multiplexer_1_out, multiplexer_3_out, PC_p6, SP_p6;
  wire [15:0] GPRA_p6, IR_p6, multiplexer_2_out, n1_bit_real_alu_1_p1, ram_1_data, undriven;

  Multiplexer #(.width(10), .enable("false")) multiplexer_1 (
    .in0(IR_p6[9:0]), .in1(adder_1_out), .out(multiplexer_1_out), .sel(in_8));
  // _10_bit_main AR: pin names not known; wires that end beside it: multiplexer_1_out, in_7, in_9, AR_p4, in_10, AR_p6
  // _16_bit_main IR: pin names not known; wires that end beside it: {IR_p1_2, IR_p1}, in_14, in_15, AR_p4, in_16, IR_p6
  Clock clock_1 (.out(AR_p4));
  // _10_bit_main PC: pin names not known; wires that end beside it: {IR_p1_2[1:0], IR_p1}, in_4, in_5, AR_p4, in_6, PC_p6
  // _10_bit_main SP: pin names not known; wires that end beside it: {IR_p1_2[1:0], IR_p1}, in_11, in_12, AR_p4, in_13, SP_p6
  Multiplexer #(.width(16), .enable("false")) multiplexer_2 (
    .in0(GPRA_p6), .in1(undriven), .out(multiplexer_2_out), .sel(in_23));
  Multiplexer #(.select(2), .width(10)) multiplexer_3 (
    .in0(PC_p6), .in1(AR_p6), .in2(SP_p6), .in3(SP_p6), .out(multiplexer_3_out), .sel(A1A0));  // open: en
  // _16_bit_main GPRA: pin names not known; wires that end beside it: {IR_p1_2, IR_p1}, in_17, in_18, AR_p4, in_20, GPRA_p6
  // _1_Bit_real_alu 1_bit_real_alu_1: pin names not known; wires that end beside it: n1_bit_real_alu_1_p1, multiplexer_2_out, n1_bit_real_alu_1_p3, S0S1S2S3, in_29, n1_bit_real_alu_1_p6, n1_bit_real_alu_1_p6
  // _8_bit_main main_1: pin names not known; wires that end beside it: AR_p4
  // _16_bit_main GPRB: pin names not known; wires that end beside it: {IR_p1_2, IR_p1}, in_19, in_21, AR_p4, in_22, GPRB_p6
  // _16_bit_main AC: pin names not known; wires that end beside it: n1_bit_real_alu_1_p3, in_26, in_28, AR_p4, in_27, n1_bit_real_alu_1_p1
  RAM #(.addrWidth(10), .dataWidth(16)) ram_1 (
    .addr(multiplexer_3_out), .data(ram_1_data), .ld(in_3), .clr(GPRB_p6));  // open: sel, clk
  // _5_bit_main X: pin names not known; wires that end beside it: X_p1, X_p2, X_p3, X_p1, X_p2, X_p3, AR_p4, X_p8, X_p8, X_p10
  Adder #(.width(10)) adder_1 (
    .a({{5{1'b0}}, X_p10}), .b({IR_p1_2[1:0], IR_p1}), .out(adder_1_out), .cin(in_24));  // open: cout
  Multiplexer #(.select(3), .width(16), .enable("false")) multiplexer_4 (
    .in0(ram_1_data), .in1({{6{1'b0}}, multiplexer_3_out}), .in2(undriven), .in3(n1_bit_real_alu_1_p1),
    .in4(GPRA_p6), .in5({{11{1'b0}}, X_p10}), .in6({{8{1'b0}}, INPR_p6}), .in7(IR_p6),
    .out({IR_p1_2, IR_p1}), .sel(D2D1D0));
  // _8_bit_main INPR: pin names not known; wires that end beside it: in_25, in_30, in_31, AR_p4, in_32, INPR_p6
  // _8_bit_main OUTR: pin names not known; wires that end beside it: IR_p1_2, IR_p1, in_34, in_35, AR_p4, in_36, out_37
endmodule
