// Logisim project HW4.circ as structural Verilog: 1 circuit, main circuit main
module main (
  input  A0,
  input  B0,
  input  A1,
  input  B1,
  input  A2,
  input  B2,
  input  A3,
  input  B3,
  input  Control_stays_as_1,
  output out_10,
  output out_11,
  output out_12,
  output out_13,
  output out_14
);

  wire adder_1_cout, adder_2_cout, adder_3_cout, xor_1_out, xor_2_out, xor_3_out, xor_4_out;

  xor xor_1 (xor_1_out, Control_stays_as_1, B0);
  xor xor_2 (xor_2_out, Control_stays_as_1, B1);
  xor xor_3 (xor_3_out, Control_stays_as_1, B2);
  xor xor_4 (xor_4_out, Control_stays_as_1, B3);
  Adder #(.width(1)) adder_1 (.a(A0), .b(xor_1_out), .out(out_10), .cin(Control_stays_as_1), .cout(adder_1_cout));
  Adder #(.width(1)) adder_2 (.a(A1), .b(xor_2_out), .out(out_11), .cin(adder_1_cout), .cout(adder_2_cout));
  Adder #(.width(1)) adder_3 (.a(A2), .b(xor_3_out), .out(out_12), .cin(adder_2_cout), .cout(adder_3_cout));
  Adder #(.width(1)) adder_4 (.a(A3), .b(xor_4_out), .out(out_13), .cin(adder_3_cout), .cout(out_14));
endmodule
