// Logisim project Experiment 5 Part 1.circ as structural Verilog: 1 circuit, main circuit main
module main (
  input  [3:0] in_1,
  input  [3:0] in_2
);

  wire [3:0] Bus_Driver__1_out;

  assign Bus_Driver__1_out = ~in_1;  // NOT_Gate Bus_Driver__1, 4 bits wide
  assign Bus_Driver__1_out = ~in_2;  // NOT_Gate Bus_Driver__2, 4 bits wide
  Pull_Resistor #(.pull(1)) pull_resistor_1 (.node(Bus_Driver__1_out[1]));
  Pull_Resistor #(.pull(1)) pull_resistor_2 (.node(Bus_Driver__1_out[3]));
  Pull_Resistor #(.pull(1)) pull_resistor_3 (.node(Bus_Driver__1_out[0]));
  Pull_Resistor #(.pull(1)) pull_resistor_4 (.node(Bus_Driver__1_out[2]));
  Hex_Digit_Display hex_digit_display_1 (.value({Bus_Driver__1_out[0], Bus_Driver__1_out[1], Bus_Driver__1_out[2], Bus_Driver__1_out[3]}));  // open: dp
endmodule
