// Logisim project Experiment 5 Part 2.circ as structural Verilog: 1 circuit, main circuit main
module main (
  input  [3:0] Data_1,
  input  [3:0] Data_2,
  input  SPDT_Switch
);

  wire not_1_out;
  wire [3:0] O1_out;

  assign O1_out = not_1_out ? Data_1 : 4'bz;  // Controlled_Buffer O1
  not not_1 (not_1_out, SPDT_Switch);
  assign O1_out = SPDT_Switch ? Data_2 : 4'bz;  // Controlled_Buffer O2
  Hex_Digit_Display hex_digit_display_1 (.value(O1_out));  // open: dp
endmodule
