// Logisim project Experiment 5 Part 3.circ as structural Verilog: 1 circuit, main circuit main
module main (
  input  [1:0] Data1,
  input  [1:0] Data2,
  input  in_3
);

  wire not_1_out, not_2_out;
  wire [1:0] controlled_buffer_1_out, controlled_buffer_3_out, controlled_buffer_4_out;

  not not_1 (not_1_out, in_3);
  assign controlled_buffer_1_out = not_1_out ? Data1 : 2'bz;  // Controlled_Buffer controlled_buffer_1
  assign controlled_buffer_1_out = in_3 ? Data2 : 2'bz;  // Controlled_Buffer controlled_buffer_2
  assign controlled_buffer_3_out = not_2_out ? controlled_buffer_1_out : 2'bz;  // Controlled_Buffer controlled_buffer_3
  not not_2 (not_2_out, in_3);
  Clock clock_1 (.out(in_3));
  assign controlled_buffer_4_out = in_3 ? controlled_buffer_1_out : 2'bz;  // Controlled_Buffer controlled_buffer_4
  Hex_Digit_Display hex_digit_display_1 (.value({controlled_buffer_4_out, controlled_buffer_3_out}));  // open: dp
endmodule
