// Logisim project Experiment 6.circ as structural Verilog: 4 circuits, main circuit main
module main (
  input  S,
  input  R,
  output QN,
  output Q
);

  nor nor_1 (QN, S, Q);
  nor nor_2 (Q, QN, R);
endmodule

module part_2 (
  input  S,
  input  C,
  input  R,
  output Q,
  output QN
);

  wire nand_1_out, nand_2_out;

  nand nand_1 (nand_1_out, S, C);
  nand nand_2 (nand_2_out, C, R);
  nand nand_3 (Q, nand_1_out, QN);
  nand nand_4 (QN, Q, nand_2_out);
endmodule

module part_3 (
  input  D,
  output Q,
  output QN
);

  wire clock_1_out, d_ff_1_q, not_1_out;

  Clock clock_1 (.out(clock_1_out));
  D_Flip_Flop d_ff_1 (.D(D), .Q(d_ff_1_q), .en(clock_1_out));  // open: clk, Qn, preset, reset
  not not_1 (not_1_out, clock_1_out);
  D_Flip_Flop d_ff_2 (.D(d_ff_1_q), .Q(Q), .Qn(QN), .en(not_1_out));  // open: clk, preset, reset
endmodule

module part_4 (
  input  [7:0] inputs,
  input  [2:0] frequency__how_far_to_shift_the_input,
  output [7:0] output__shifted_input
);

  Shifter shifter_1 (.in(inputs), .\dist (frequency__how_far_to_shift_the_input), .out(output__shifted_input));
endmodule
